# Fritzing sketch shema spajanja razvojnog sistema (saved by Fritzing 0.9.3b)
breadboards: 1

parts:
  S1 = Pushbutton [package="[THT]"]
  S2 = Pushbutton [package="[THT]"]
  S3 = Pushbutton [package="[THT]"]
  S4 = Pushbutton [package="[THT]"]
  MBED1 = mbed
  U1 = Nokia 6100 Color LCD [package=nokia6100_lcd]
  U2 = POT_SWITCH [package=pot_pth_switch]
  U3 = POT_SWITCH [package=pot_pth_switch]
  R1 = Resistor [tolerance=±5% resistance=220 package=THT]
  R5 = Resistor [tolerance=±5% resistance=220 package=THT]
  R6 = Resistor [tolerance=±5% resistance=220 package=THT]
  R7 = Resistor [tolerance=±5% resistance=220 package=THT]

nets:
  N1: S1.Pin_1, S1.Pin_2, S2.Pin_1, S2.Pin_2, S3.Pin_1, S3.Pin_2, S4.Pin_1, S4.Pin_2, MBED1.Vin, U2.G$1_E, U3.G$1_S, U3.G$1_E
  N2: S1.Pin_3, S1.Pin_4, R6.Pin_1
  N3: S2.Pin_3, S2.Pin_4, R5.Pin_1
  N4: S3.Pin_3, S3.Pin_4, R1.Pin_1
  N5: S4.Pin_3, S4.Pin_4, R7.Pin_1
  N6: MBED1.GND, U2.G$1_A, U3.G$1_A, R1.Pin_0, R5.Pin_0, R6.Pin_0, R7.Pin_0
  N7: MBED1.pin25, U1.CS
  N8: MBED1.pin26, U1.SCK
  N9: MBED1.pin27, U1.DIO
  N10: MBED1.pin28, U1.RESET
  N11: MBED1.pin29, U1.VDIGITAL
